# Fritzing sketch EEPROM-test-hookup (saved by Fritzing 0.9.2b)
breadboards: 1

parts:
  Raspberry_Pi1 = Raspberry Pi B+
  Part1 = Bi-Directional Logic Level Converter [part_number=BOB-12009]  # not connected
  EEPROM = IC, DIP package, 8 pins [chip_label=IC]

nets:
  N1: Raspberry_Pi1.GND, EEPROM.pin1, EEPROM.pin3, EEPROM.pin4, EEPROM.pin7
  N2: Raspberry_Pi1.5V, EEPROM.pin2, EEPROM.pin8

custom parts:
  Bi-Directional Logic Level Converter: Description: If you've ever tried to connect a 3.3V device to a 5V system, you know what a challenge it can be. The SparkFun bi-directional logic level converter is a small device that safely steps down 5V signals to 3.3V AND steps up 3.3V to 5V at the same time. This level converter also works with 2.8V and 1.8V devices. What really separates this Logic level converter from our previous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
